// Logisim project alu_4bit_processor.circ as structural Verilog: 1 circuit, main circuit main
module main (
  input  [3:0] INPUT_A,
  input  [3:0] INPUT_B,
  input  [2:0] OPCODE,
  input  LOAD_EN,
  input  RST,
  output FLAG_CARRY,
  output [3:0] RESULT_OUT,
  output FLAG_ZERO
);

  wire CLK_out;
  wire [3:0] adder_1_out, adder_2_out, and_1_out, multiplexer_1_out, not_1_out, or_1_out, REG_A_q, REG_B_q,
       subtractor_1_out, xor_1_out;

  Clock CLK (.out(CLK_out));
  Register #(.width(4)) REG_A (.D(INPUT_A), .en(CLK_out), .clk(LOAD_EN), .Q(REG_A_q));  // open: clr
  Register #(.width(4)) REG_B (.D(INPUT_B), .en(CLK_out), .clk(LOAD_EN), .Q(REG_B_q));  // open: clr
  Adder #(.width(4)) adder_1 (.a(REG_A_q), .b(REG_B_q), .out(adder_1_out), .cin(FLAG_CARRY));  // open: cout
  Subtractor #(.width(4)) subtractor_1 (.a(REG_A_q), .b(REG_B_q), .out(subtractor_1_out));  // open: bin, bout
  // AND_Gate and_1 has open pins: out=and_1_out
  // OR_Gate or_1 has open pins: out=or_1_out
  // XOR_Gate xor_1 has open pins: out=xor_1_out
  assign not_1_out = ~REG_A_q;  // NOT_Gate not_1, 4 bits wide
  Adder #(.width(4)) adder_2 (.a(REG_A_q), .b(4'b0001), .out(adder_2_out));  // open: cin, cout
  Multiplexer #(.select(3), .width(4)) multiplexer_1 (
    .in0(adder_1_out), .in1(subtractor_1_out), .in2(and_1_out), .in3(or_1_out), .in4(xor_1_out),
    .in5(not_1_out), .in6(adder_2_out), .in7(4'b0000), .out(multiplexer_1_out), .sel(OPCODE));
  Register #(.width(4)) ACC_RESULT (.D(multiplexer_1_out), .en(CLK_out), .clk(LOAD_EN), .Q(RESULT_OUT));  // open: clr
  Hex_Digit_Display HEX_DISP ();  // open: value, dp
  Comparator #(.mode("unsigned"), .width(4)) comparator_1 (.a(RESULT_OUT), .eq(FLAG_ZERO));  // open: b, gt, lt
endmodule
