// Logisim project dual_mode_8bit_alu_processor.circ as structural Verilog: 1 circuit, main circuit main
module main (
  input  MODE_COMPUTE_VERIFY,
  input  [7:0] OPERAND_A_8BIT,
  input  [7:0] OPERAND_B_8BIT,
  input  [2:0] OPCODE,
  input  LOAD_EN,
  input  RST,
  output VERIFY_PASS_MATCH,
  output [7:0] RESULT_8BIT_OUT,
  output FLAG_CARRY_8BIT,
  output FLAG_ZERO
);

  wire CLK_out;
  wire [3:0] adder_1_p4, adder_2_p4, and_1_out, and_2_out, multiplexer_1_out, multiplexer_2_out,
       multiplexer_3_out, multiplexer_4_out, or_1_out, or_2_out, xor_1_out, xor_2_out;
  wire [7:0] REG_A_q, REG_B_q;

  Clock CLK (.out(CLK_out));
  Register #(.width(8)) REG_A (.D(OPERAND_A_8BIT), .en(CLK_out), .clk(LOAD_EN), .Q(REG_A_q));  // open: clr
  Register #(.width(8)) REG_B (.D(OPERAND_B_8BIT), .en(CLK_out), .clk(LOAD_EN), .Q(REG_B_q));  // open: clr
  Multiplexer #(.width(4)) multiplexer_1 (
    .in0(REG_A_q[7:4]), .in1(REG_A_q[3:0]), .out(multiplexer_1_out), .sel(MODE_COMPUTE_VERIFY));
  Multiplexer #(.width(4)) multiplexer_2 (
    .in0(REG_B_q[7:4]), .in1(REG_B_q[3:0]), .out(multiplexer_2_out), .sel(MODE_COMPUTE_VERIFY));
  // Adder #(.width(4)) adder_1: pin names not known; wires that end beside it: REG_A_q[3:0], REG_B_q[3:0], FLAG_CARRY_8BIT, adder_1_p4
  // AND_Gate and_1 has open pins: out=and_1_out
  // OR_Gate or_1 has open pins: out=or_1_out
  // XOR_Gate xor_1 has open pins: out=xor_1_out
  // Adder #(.width(4)) adder_2: pin names not known; wires that end beside it: multiplexer_1_out, multiplexer_2_out, FLAG_CARRY_8BIT, adder_2_p4
  // AND_Gate and_2 has open pins: out=and_2_out
  // OR_Gate or_2 has open pins: out=or_2_out
  // XOR_Gate xor_2 has open pins: out=xor_2_out
  Multiplexer #(.select(3), .width(4)) multiplexer_3 (
    .in0(adder_1_p4), .in4(and_1_out), .out(multiplexer_3_out), .sel(OPCODE));  // open: in1, in2, in3, in5, in6, in7
  Multiplexer #(.select(3), .width(4)) multiplexer_4 (
    .in0(adder_2_p4), .in4(and_2_out), .out(multiplexer_4_out), .sel(OPCODE));  // open: in1, in2, in3, in5, in6, in7
  Comparator #(.mode("unsigned"), .width(4)) comparator_1 (
    .a(multiplexer_3_out), .b(multiplexer_4_out), .eq(VERIFY_PASS_MATCH));  // open: gt, lt
  Register #(.width(8)) ACC_RESULT_8BIT (
    .D({multiplexer_4_out, multiplexer_3_out}), .en(CLK_out), .clk(LOAD_EN), .Q(RESULT_8BIT_OUT));  // open: clr
  LED LED_PASS (.in(VERIFY_PASS_MATCH));
  Comparator #(.mode("unsigned"), .width(8)) comparator_2 (.a(RESULT_8BIT_OUT), .eq(FLAG_ZERO));  // open: b, gt, lt
  Hex_Digit_Display HEX_UPPER ();  // open: value, dp
  Hex_Digit_Display HEX_LOWER ();  // open: value, dp
endmodule
